# Fritzing sketch esp8266-button-circuit-diagram (saved by Fritzing 0.9.4)
breadboards: 1

parts:
  WeMos_D1_Mini2 = WeMos D1 Mini
  S1 = Pushbutton [package="[THT]"]

nets:
  N1: WeMos_D1_Mini2.D5, S1.Pin_3, S1.Pin_4
  N2: WeMos_D1_Mini2.G, S1.Pin_1, S1.Pin_2
