# Fritzing sketch esp8266-led-button-circuit-diagram (saved by Fritzing 0.9.4)
breadboards: 1

parts:
  WeMos_D1_Mini2 = WeMos D1 Mini
  S1 = Pushbutton [package="[THT]"]
  R1 = Resistor [tolerance=±5% resistance=330 package=THT]
  LED1 = LED - 5mm [color="Red (633nm)" package="5 mm [THT]"]

nets:
  N1: WeMos_D1_Mini2.D1, LED1.anode
  N2: WeMos_D1_Mini2.D5, S1.Pin_3, S1.Pin_4
  N3: WeMos_D1_Mini2.G, S1.Pin_1, S1.Pin_2, R1.Pin_1
  N4: R1.Pin_0, LED1.cathode
